// Logisim project Pipelined Multiplier Logisim .circ as structural Verilog: 1 circuit, main circuit main
module main (
  input  Reset,
  input  Clear,
  input  in_3,
  input  [31:0] Input_1,
  input  [31:0] Input_2,
  input  RegWrite,
  output [31:0] Output
);

  wire Global_Clock_out, register_3_q, register_4_q;
  wire [4:0] multiplexer_3_out, multiplexer_4_out;
  wire [7:0] Program_Counter_q;
  wire [31:0] adder_1_out, EX_Result_Register_q, Instruction_Register_q, multiplexer_1_out,
       multiplexer_2_out, multiplier_1_out, ram_1_data, ram_2_data, register_1_q, register_2_q, rom_1_data;
  wire [31:8] Program_Counter_q_2;

  Clock Global_Clock (.out(Global_Clock_out));
  Register #(.width(32)) Program_Counter (
    .D(adder_1_out), .Q({Program_Counter_q_2, Program_Counter_q}), .clk(Global_Clock_out), .clr(Reset));  // open: en
  ROM #(.dataWidth(32)) rom_1 (.addr(Program_Counter_q), .data(rom_1_data));  // open: sel
  Register #(.width(32)) register_1 (.D(Input_1), .Q(register_1_q), .clk(Global_Clock_out), .clr(Reset));  // open: en
  Register #(.width(32)) Instruction_Register (
    .D(rom_1_data), .Q(Instruction_Register_q), .clk(Global_Clock_out), .clr(Reset));  // open: en
  Adder #(.width(32)) adder_1 (
    .a({Program_Counter_q_2, Program_Counter_q}), .b(32'h1), .out(adder_1_out));  // open: cin, cout
  Multiplexer #(.width(32)) multiplexer_1 (
    .in0(Output), .in1(register_1_q), .out(multiplexer_1_out), .sel(RegWrite));  // open: en
  Multiplexer #(.width(32)) multiplexer_2 (
    .in0(Output), .in1(register_2_q), .out(multiplexer_2_out), .sel(RegWrite));  // open: en
  RAM #(.addrWidth(5), .dataWidth(32), .bus("separate")) ram_1 (
    .addr(multiplexer_3_out), .din(multiplexer_1_out), .data(ram_1_data), .sel(in_3), .clk(Global_Clock_out),
    .clr(Clear));  // open: str, ld
  RAM #(.addrWidth(5), .dataWidth(32), .bus("separate")) ram_2 (
    .addr(multiplexer_4_out), .din(multiplexer_2_out), .data(ram_2_data), .sel(in_3), .clk(Global_Clock_out),
    .clr(Clear));  // open: str, ld
  Register #(.width(32)) register_2 (.D(Input_2), .Q(register_2_q), .clk(Global_Clock_out), .clr(Reset));  // open: en
  Multiplexer #(.width(5)) multiplexer_3 (
    .in0(Instruction_Register_q[25:21]), .in1(Instruction_Register_q[15:11]), .out(multiplexer_3_out),
    .sel(register_4_q));  // open: en
  Multiplexer #(.width(5)) multiplexer_4 (
    .in0(Instruction_Register_q[20:16]), .in1(Instruction_Register_q[15:11]), .out(multiplexer_4_out),
    .sel(register_4_q));  // open: en
  Register #(.width(1)) register_3 (.D(1'b1), .Q(register_3_q), .clk(Global_Clock_out), .clr(Reset));  // open: en
  Multiplier #(.width(32)) multiplier_1 (.a(ram_1_data), .b(ram_2_data), .out(multiplier_1_out));  // open: cin, cout
  Register #(.width(1)) register_4 (
    .D(register_3_q), .Q(register_4_q), .clk(Global_Clock_out), .clr(Reset));  // open: en
  Register #(.width(32)) EX_Result_Register (
    .D(multiplier_1_out), .Q(EX_Result_Register_q), .clk(Global_Clock_out), .clr(Reset));  // open: en
  Register #(.width(32)) MEM_WB_Register (
    .D(EX_Result_Register_q), .Q(Output), .clk(Global_Clock_out), .clr(Reset));  // open: en

  // Notes on the sheet:
  //   contents of rom_1 (hex, n*v repeats v):
  //   8446000
  //   rd_WB
  //   rs
  //   rt
  //   ReadData1
  //   ReadData2
endmodule
